// Logisim project 8bit_cpu.circ as structural Verilog: 3 circuits, main circuit ULA
module ULA (
  input  [7:0] A,
  input  [7:0] B,
  input  [2:0] Select_Op,
  output [7:0] out_4
);

  wire [7:0] adder_1_out, adder_2_out, adder_3_out, and_1_out, or_1_out, subtractor_1_out;

  Adder adder_1 (.a(A), .b(8'h1), .out(adder_1_out));  // open: cin, cout
  Adder adder_2 (.a(B), .b(8'h1), .out(adder_2_out));  // open: cin, cout
  Adder adder_3 (.a(A), .b(B), .out(adder_3_out));  // open: cin, cout
  Subtractor subtractor_1 (.a(A), .b(B), .out(subtractor_1_out));  // open: bin, bout
  assign and_1_out = A & A;  // AND_Gate and_1, 8 bits wide
  assign or_1_out = A | B;  // OR_Gate or_1, 8 bits wide
  Multiplexer #(.select(3), .width(8)) multiplexer_1 (
    .in0(A), .in1(B), .in2(adder_1_out), .in3(adder_2_out), .in4(adder_3_out), .in5(subtractor_1_out),
    .in6(and_1_out), .in7(or_1_out), .out(out_4), .sel(Select_Op));  // open: en
endmodule

module Datapath (
  input  Program_Counter_Register_Enable,
  input  [7:0] External_Memory_Data_Bus,
  input  Memory_Byte_Register_Enable,
  input  Register_Output_Enable,
  input  Register_B_Enable,
  input  [7:0] External_Input,
  input  Register_A_Enablel,
  input  [1:0] MUX_Fonte_B,
  input  [2:0] AluOp,
  output [7:0] External_Memory_Address_Bus,
  output [7:0] ULA_Output
);

  wire Clock_out, Reset_Registers_out;
  wire [7:0] Memory_Byte_Register_q, multiplexer_1_out, Register_A_q, Register_B_q;

  Clock Clock (.out(Clock_out));
  Register Program_Counter (
    .D(ULA_Output), .en(Program_Counter_Register_Enable), .Q(External_Memory_Address_Bus), .clk(Clock_out),
    .clr(Reset_Registers_out));
  Register Output (.D(ULA_Output), .en(Register_Output_Enable), .clk(Clock_out), .clr(Reset_Registers_out));  // open: Q
  Register Register_B (
    .D(ULA_Output), .en(Register_B_Enable), .Q(Register_B_q), .clk(Clock_out), .clr(Reset_Registers_out));
  Register Register_A (
    .D(ULA_Output), .en(Register_A_Enablel), .Q(Register_A_q), .clk(Clock_out), .clr(Reset_Registers_out));
  Clock Reset_Registers (.out(Reset_Registers_out));
  Register Memory_Byte_Register (
    .D(External_Memory_Data_Bus), .en(Memory_Byte_Register_Enable), .Q(Memory_Byte_Register_q),
    .clk(Clock_out), .clr(Reset_Registers_out));
  Multiplexer #(.select(2), .width(8)) multiplexer_1 (
    .in0(Register_B_q), .in1(Memory_Byte_Register_q), .in2(External_Memory_Address_Bus),
    .in3(External_Input), .out(multiplexer_1_out), .sel(MUX_Fonte_B), .en(1'b1));
  ULA ula_1 (.out_4(ULA_Output), .A(Register_A_q), .B(multiplexer_1_out), .Select_Op(AluOp));
endmodule

module Principal (
  input  [7:0] External_Input,
  input  [7:0] External_Memory_Data,
  output [7:0] External_Memory_Address,
  output [15:0] out_4
);

  wire clock_1_out;
  wire [4:0] bit_extender_1_out, MPC_q, multiplexer_1_out;
  wire [7:0] datapath_1_ula_output;
  wire [15:0] rom_1_data;

  Datapath datapath_1 (
    .Program_Counter_Register_Enable(out_4[6]), .External_Memory_Data_Bus(External_Memory_Data),
    .Memory_Byte_Register_Enable(out_4[5]), .Register_Output_Enable(out_4[4]), .Register_B_Enable(out_4[3]),
    .Register_A_Enablel(out_4[2]), .External_Memory_Address_Bus(External_Memory_Address),
    .MUX_Fonte_B(out_4[1:0]), .AluOp(out_4[9:7]), .ULA_Output(datapath_1_ula_output),
    .External_Input(External_Input));
  Bit_Extender #(.out_width(5)) bit_extender_1 (.in(datapath_1_ula_output), .out(bit_extender_1_out));
  Register #(.width(5)) MPC (.D(multiplexer_1_out), .Q(MPC_q), .clk(clock_1_out));  // open: en, clr
  Multiplexer #(.width(5)) multiplexer_1 (
    .in0(out_4[15:11]), .in1(bit_extender_1_out), .out(multiplexer_1_out), .sel(out_4[10]));  // open: en
  ROM #(.addrWidth(5), .dataWidth(16)) rom_1 (.addr(MPC_q), .data(rom_1_data));  // open: sel
  Register #(.width(16)) MIR (.D(rom_1_data), .Q(out_4), .clk(clock_1_out));  // open: en, clr
  Clock clock_1 (.out(clock_1_out));

  // Notes on the sheet:
  //   contents of rom_1 (hex, n*v repeats v):
  //   12
endmodule
